# Fritzing sketch test_8x8led (saved by Fritzing 0.9.2b)

parts:
  元件1 = Arduino Uno (Rev3) - ICSP
  Disp1 = Max7219 8x8 [part_number=LBT2088AH]

nets:
  N1: 元件1.D2, Disp1.DIN
  N2: 元件1.D3_PWM, Disp1.CS
  N3: 元件1.D4, Disp1.CLK
  5V: 元件1.5V, Disp1.VCC
  GND: 元件1.GND, Disp1.GND

custom parts:
  Max7219 8x8: LED Matrix Display 8x8 red 60.5mm
